# Fritzing sketch ContRegressiva (saved by Fritzing 0.9.3b)
breadboards: 1

parts:
  WeMos_D1_Mini1 = WeMos D1 Mini
  U1 = MAX7219 [package=dil24]
  D1 = LED_BARGRAPH_10 [package=led_bargaph_10]
  D2 = LED_BARGRAPH_10 [package=led_bargaph_10]
  R1 = Resistor [tolerance=±5% resistance=82k package=THT]

nets:
  5V: WeMos_D1_Mini1.5V, U1.VCC, R1.Pin_0
  N1: WeMos_D1_Mini1.D2, U1.CLK
  N2: WeMos_D1_Mini1.D3, U1.LOAD
  N3: WeMos_D1_Mini1.D4, U1.DIN
  GND: WeMos_D1_Mini1.G, U1.GND, U1.GND2
  N4: U1.DIG0, D2.C_A, D2.D_A, D2.E_A, D2.F_A, D2.G_A, D2.H_A, D2.I_A, D2.J_A
  N5: U1.DIG1, D1.C_A, D1.D_A, D1.E_A, D1.F_A, D1.G_A, D1.H_A, D1.I_A, D1.J_A
  N6: U1.SEGA, D1.D_C, D2.D_C
  N7: U1.SEGF, D1.I_C, D2.I_C
  N8: U1.SEGB, D1.E_C, D2.E_C
  N9: U1.SEGG, D1.J_C, D2.J_C
  N10: U1.ISET, R1.Pin_1
  N11: U1.SEGC, D1.F_C, D2.F_C
  N12: U1.SEGE, D1.H_C, D2.H_C
  N13: U1.SEGDP, D1.C_C, D2.C_C
  N14: U1.SEGD, D1.G_C, D2.G_C
